# Fritzing sketch 3WDTrashBase (saved by Fritzing 0.9.5d)

parts:
  S2 = H-Bridge with L298N
  VCC1 = Battery
  DC_Mot_Enc1 = DC Motor with two-phase hall-encoder [part_number=VT-E-G25A-06-177E]
  DC_Mot_Enc3 = DC Motor with two-phase hall-encoder [part_number=VT-E-G25A-06-177E]
  S1 = H-Bridge with L298N
  Mod1 = Raspberry Pi 4B
  DC_Mot_Enc5 = DC Motor with two-phase hall-encoder [part_number=VT-E-G25A-06-177E]

nets:
  12V: S2.12V, VCC1.+, S1.12V
  GND: S2.GND, VCC1.-, DC_Mot_Enc1.pin5, DC_Mot_Enc3.pin5, S1.GND, DC_Mot_Enc5.pin5
  N1: S2.5V, DC_Mot_Enc1.pin2
  N2: S2.IN1, Mod1.GPIO15
  N3: S2.IN2, Mod1.GPIO18
  N4: S2.M1-01, DC_Mot_Enc1.pin1
  N5: S2.M1-02, DC_Mot_Enc1.pin6
  N6: S2.ENA, Mod1.GPIO14
  N7: DC_Mot_Enc1.pin3, Mod1.GPIO20
  N8: DC_Mot_Enc1.pin4, Mod1.GPIO21
  N9: DC_Mot_Enc3.pin1, S1.M1-01
  N10: DC_Mot_Enc3.pin2, S1.5V, DC_Mot_Enc5.pin2
  N11: DC_Mot_Enc3.pin3, Mod1.GPIO6
  N12: DC_Mot_Enc3.pin4, Mod1.GPIO5
  N13: DC_Mot_Enc3.pin6, S1.M1-02
  N14: S1.IN1, Mod1.GPIO27
  N15: S1.IN2, Mod1.GPIO17
  N16: S1.IN3, Mod1.GPIO4
  N17: S1.IN4, Mod1.GPIO3
  N18: S1.M1-03, DC_Mot_Enc5.pin6
  N19: S1.M1-04, DC_Mot_Enc5.pin1
  N20: S1.ENA, Mod1.GPIO22
  N21: S1.ENB, Mod1.GPIO2
  N22: Mod1.GPIO13, DC_Mot_Enc5.pin4
  N23: Mod1.GPIO19, DC_Mot_Enc5.pin3

custom parts:
  H-Bridge with L298N: h-bridge
  Battery: Your standard 3x 18650 battery pack (12 Volts)
